# Fritzing sketch Untitled Sketch (saved by Fritzing 0.9.3b)

parts:
  Componente2 = Adafruit LSM9DS1 9DoF Breakout [part_number="Adafruit #3387"]
  Componente3 = Adafruit Metro M0 Express

nets:
  N1: Componente2.SDA, Componente3.SDA
  N2: Componente2.SCL, Componente3.SCL
  GND: Componente2.GND, Componente3.GND
  VDD: Componente2.VDD, Componente3.3.3V

custom parts:
  Adafruit LSM9DS1 9DoF Breakout: Add motion, direction and orientation sensing to your Arduino project with this all-in-one 9-DOF sensor. Inside the chip are three sensors, one is a classic 3-axis accelerometer, which can tell you which direction is down towards the Earth (by measuring gravity) or how fast the board is accelerating in 3D space. The other is a 3-axis magnetometer that can sense where the strongest magnetic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
  Adafruit Metro M0 Express: Metro is our series of microcontroller boards for use with the Arduino IDE. This new Metro board looks a whole lot like our original Metro 328, but with a huge upgrade. Instead of the ATmega328, this Metro features a ATSAMD21G18 chip, an ARM Cortex M0+. It's our first Metro that is designed for use with CircuitPython! CircuitPython is our beginner-oriented flavor of MicroPython - and as the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
